# Fritzing sketch model (saved by Fritzing 0.9.2b)
breadboards: 1

parts:
  Part1 = Arduino Uno (Rev3)
  LED3 = smd LED [color="Green (555nm)" package="1206 [SMD]"]
  R6 = Resistor [tolerance=±5% resistance=10k package=THT]
  R1 = Resistor [tolerance=±5% resistance=10k package=THT]
  S3 = Pushbutton [package="[THT]"]
  LED2 = smd LED [color="Blue (430nm)" package="1206 [SMD]"]
  LED1 = smd LED [color="Red (633nm)" package="1206 [SMD]"]
  S2 = Pushbutton [package="[THT]"]
  S1 = Pushbutton [package="[THT]"]
  R5 = Resistor [tolerance=±5% resistance=10k package=THT]  # not connected
  R2 = Resistor [tolerance=±5% resistance=10k package=THT]
  R4 = Resistor [tolerance=±5% resistance=10k package=THT]
  R3 = Resistor [tolerance=±5% resistance=10k package=THT]
  R7 = Resistor [tolerance=±5% resistance=10k package=THT]
  R8 = Resistor [tolerance=±5% resistance=10k package=THT]
  S4 = Pushbutton [package="[THT]"]
  LED4 = smd LED [color="Yellow (585nm)" package="1206 [SMD]"]

nets:
  N1: Part1.D8, Part1.D9_PWM, Part1.D10_PWM/SS, Part1.5V, S2.Pin_3, S2.Pin_4, S1.Pin_3, S1.Pin_4, S4.Pin_3, S4.Pin_4
  N2: Part1.D11_PWM/MOSI, S3.Pin_3, S3.Pin_4
  N3: Part1.D2, R1.Pin_1
  N4: Part1.D3_PWM, R7.Pin_1
  N5: Part1.D4, R3.Pin_1
  N6: Part1.GND, R6.Pin_1, R2.Pin_1, R4.Pin_1, R8.Pin_1
  N7: LED3.cathode, LED2.cathode, LED1.cathode, LED4.cathode
  N8: LED3.anode, R3.Pin_0
  N9: R6.Pin_0, S3.Pin_1, S3.Pin_2
  N10: R1.Pin_0, LED1.anode
  N11: LED2.anode, R7.Pin_0
  N12: S2.Pin_1, S2.Pin_2, R4.Pin_0
  N13: S1.Pin_1, S1.Pin_2, R2.Pin_0
  N14: R8.Pin_0, S4.Pin_1, S4.Pin_2
